# Fritzing sketch Stm32-VFO (saved by Fritzing 0.9.3b)
breadboards: 1

parts:
  U1 = BluePill
  TFT_1_8"_ST7735S = ST7735 1.8 inch TFT LCD [package="SIP (Single Inline) [THT]"]
  Part1 = Adafruit Si5351A Clock Generator [part_number="Adafruit #2045"]

nets:
  N1: U1.B10, Part1.SCL
  N2: U1.B11, Part1.SDA
  3V3: U1.3V3, TFT_1_8"_ST7735S.VCC, Part1.VIN
  GND: U1.GND, TFT_1_8"_ST7735S.GND, Part1.GND
  N3: U1.B4, TFT_1_8"_ST7735S.LED
  N4: U1.A12, TFT_1_8"_ST7735S.CS
  N5: U1.A10, TFT_1_8"_ST7735S.RST
  N6: U1.A9, TFT_1_8"_ST7735S.A0
  N7: U1.B15, TFT_1_8"_ST7735S.SDA
  N8: U1.B13, TFT_1_8"_ST7735S.SCK

custom parts:
  ST7735 1.8 inch TFT LCD: 1.8 inch TFT LCD module. SPI interface, ST7735 controller
  Adafruit Si5351A Clock Generator: Never hunt around for another crystal again, with the Si5351A clock generator breakout from Adafruit! This chip has a precision 25MHz crystal reference and internal PLL and dividers so it can generate just about any frequency, from <8KHz up to 150+ MHz. The Si5351A clock generator is an I2C controller clock generator. It uses the onboard precision clock to drive multiple PLL's and clock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
